// Logisim project ALUCU.circ as structural Verilog: 2 circuits, main circuit main
module main (
);

  wire [2:0] ALU_CU_aluoperation;

  ALU_CU ALU_CU (.ALU_op(2'b01), .FunctionCode(6'b101010), .ALUOperation(ALU_CU_aluoperation));
  // Probe on ALU_CU_aluoperation

  // Notes on the sheet:
  //   FunctionCode(6 bit hex value)
  //   ALUOP(Hex value)
  //   ALUOperation(3-bit hex value)
endmodule

module ALU_CU (
  input  [1:0] ALU_op,
  input  [5:0] FunctionCode,
  output [2:0] ALUOperation
);

  wire and_1_out, not_1_out, not_2_out, or_1_out;

  or or_1 (or_1_out, FunctionCode[0], FunctionCode[3]);
  and and_1 (and_1_out, ALU_op[1], FunctionCode[1]);
  and and_2 (ALUOperation[0], ALU_op[1], or_1_out);
  or or_2 (ALUOperation[2], ALU_op[0], and_1_out);
  not not_1 (not_1_out, ALU_op[1]);
  or or_3 (ALUOperation[1], not_1_out, not_2_out);
  not not_2 (not_2_out, FunctionCode[2]);

  // Notes on the sheet:
  //   Operation0
  //   Operation2
  //   Operation1
endmodule
