// Logisim project RegFile.circ as structural Verilog: 2 circuits, main circuit main
module main (
  output [31:0] ReadData1,
  output [31:0] ReadData2
);

  wire clock_1_out;

  Clock clock_1 (.out(clock_1_out));
  RegFile regfile_1 (
    .ReadReg1({5{1'b0}}), .ReadReg2(5'b00001), .WRITE(1'b0), .clock(clock_1_out), .WriteRegister(5'b00001),
    .WriteData(32'h55f9), .ReadData1(ReadData1), .ReadData2(ReadData2));

  // Notes on the sheet:
  //   Read Reg2
  //   write
  //   Clock
  //   WriteReg
  //   WriteData
endmodule

module RegFile (
  input  [4:0] ReadReg1,
  input  [4:0] ReadReg2,
  input  WRITE,
  input  clock,
  input  [4:0] WriteRegister,
  input  [31:0] WriteData,
  output [31:0] ReadData1,
  output [31:0] ReadData2
);

  wire AND_gate_2_out, AND_gate_3_out, AND_gate_4_out, AND_gate_5_out, AND_gate_6_out, AND_gate_7_out,
       AND_gate_8_out, AND_gate_9_out, AND_gate_10_out, AND_gate_11_out, AND_gate_12_out, AND_gate_13_out,
       AND_gate_14_out, AND_gate_15_out, AND_gate_16_out, AND_gate_17_out, AND_gate_18_out, AND_gate_19_out,
       AND_gate_20_out, AND_gate_21_out, AND_gate_22_out, AND_gate_23_out, AND_gate_24_out, AND_gate_25_out,
       AND_gate_26_out, AND_gate_27_out, AND_gate_28_out, AND_gate_29_out, AND_gate_30_out, AND_gate_31_out,
       AND_gate_32_out, AND_gate_out, decoder_1_out0, decoder_1_out1, decoder_1_out2, decoder_1_out3,
       decoder_1_out4, decoder_1_out5, decoder_1_out6, decoder_1_out7, decoder_1_out8, decoder_1_out9,
       decoder_1_out10, decoder_1_out11, decoder_1_out12, decoder_1_out13, decoder_1_out14, decoder_1_out15,
       decoder_1_out16, decoder_1_out17, decoder_1_out18, decoder_1_out19, decoder_1_out20, decoder_1_out21,
       decoder_1_out22, decoder_1_out23, decoder_1_out24, decoder_1_out25, decoder_1_out26, decoder_1_out27,
       decoder_1_out28, decoder_1_out29, decoder_1_out30, decoder_1_out31;
  wire [31:0] reg0_q, reg1_q, reg2_q, reg3_q, reg4_q, reg5_q, reg6_q, reg7_q, reg8_q, reg9_q, reg10_q,
       reg11_q, reg12_q, reg13_q, reg14_q, reg15_q, reg16_q, reg17_q, reg18_q, reg19_q, reg20_q, reg21_q,
       reg22_q, reg23_q, reg24_q, reg25_q, reg26_q, reg27_q, reg28_q, reg29_q, reg30_q, reg31_q;

  Decoder #(.select(5), .enable("false")) decoder_1 (
    .out0(decoder_1_out0), .out1(decoder_1_out1), .out2(decoder_1_out2), .out3(decoder_1_out3),
    .out4(decoder_1_out4), .out5(decoder_1_out5), .out6(decoder_1_out6), .out7(decoder_1_out7),
    .out8(decoder_1_out8), .out9(decoder_1_out9), .out10(decoder_1_out10), .out11(decoder_1_out11),
    .out12(decoder_1_out12), .out13(decoder_1_out13), .out14(decoder_1_out14), .out15(decoder_1_out15),
    .out16(decoder_1_out16), .out17(decoder_1_out17), .out18(decoder_1_out18), .out19(decoder_1_out19),
    .out20(decoder_1_out20), .out21(decoder_1_out21), .out22(decoder_1_out22), .out23(decoder_1_out23),
    .out24(decoder_1_out24), .out25(decoder_1_out25), .out26(decoder_1_out26), .out27(decoder_1_out27),
    .out28(decoder_1_out28), .out29(decoder_1_out29), .out30(decoder_1_out30), .out31(decoder_1_out31),
    .sel(WriteRegister));
  and AND_gate (AND_gate_out, WRITE, decoder_1_out0);
  and AND_gate_2 (AND_gate_2_out, WRITE, decoder_1_out1);
  and AND_gate_3 (AND_gate_3_out, WRITE, decoder_1_out2);
  and AND_gate_4 (AND_gate_4_out, WRITE, decoder_1_out3);
  and AND_gate_5 (AND_gate_5_out, WRITE, decoder_1_out4);
  and AND_gate_6 (AND_gate_6_out, WRITE, decoder_1_out5);
  and AND_gate_7 (AND_gate_7_out, WRITE, decoder_1_out6);
  and AND_gate_8 (AND_gate_8_out, WRITE, decoder_1_out7);
  and AND_gate_9 (AND_gate_9_out, WRITE, decoder_1_out8);
  and AND_gate_10 (AND_gate_10_out, WRITE, decoder_1_out9);
  and AND_gate_11 (AND_gate_11_out, WRITE, decoder_1_out10);
  and AND_gate_12 (AND_gate_12_out, WRITE, decoder_1_out11);
  and AND_gate_13 (AND_gate_13_out, WRITE, decoder_1_out12);
  and AND_gate_14 (AND_gate_14_out, WRITE, decoder_1_out13);
  and AND_gate_15 (AND_gate_15_out, WRITE, decoder_1_out14);
  and AND_gate_16 (AND_gate_16_out, WRITE, decoder_1_out15);
  and AND_gate_17 (AND_gate_17_out, WRITE, decoder_1_out16);
  and AND_gate_18 (AND_gate_18_out, WRITE, decoder_1_out17);
  and AND_gate_19 (AND_gate_19_out, WRITE, decoder_1_out18);
  and AND_gate_20 (AND_gate_20_out, WRITE, decoder_1_out19);
  and AND_gate_21 (AND_gate_21_out, WRITE, decoder_1_out20);
  and AND_gate_22 (AND_gate_22_out, WRITE, decoder_1_out21);
  and AND_gate_23 (AND_gate_23_out, WRITE, decoder_1_out22);
  and AND_gate_24 (AND_gate_24_out, WRITE, decoder_1_out23);
  and AND_gate_25 (AND_gate_25_out, WRITE, decoder_1_out24);
  and AND_gate_26 (AND_gate_26_out, WRITE, decoder_1_out25);
  and AND_gate_27 (AND_gate_27_out, WRITE, decoder_1_out26);
  and AND_gate_28 (AND_gate_28_out, WRITE, decoder_1_out27);
  and AND_gate_29 (AND_gate_29_out, WRITE, decoder_1_out28);
  and AND_gate_30 (AND_gate_30_out, WRITE, decoder_1_out29);
  and AND_gate_31 (AND_gate_31_out, WRITE, decoder_1_out30);
  and AND_gate_32 (AND_gate_32_out, WRITE, decoder_1_out31);
  Register #(.width(32)) reg0 (.D(WriteData), .en(AND_gate_out), .Q(reg0_q), .clk(clock));  // open: clr
  Register #(.width(32)) reg1 (.D(WriteData), .en(AND_gate_2_out), .Q(reg1_q), .clk(clock));  // open: clr
  Register #(.width(32)) reg2 (.D(WriteData), .en(AND_gate_3_out), .Q(reg2_q), .clk(clock));  // open: clr
  Register #(.width(32)) reg3 (.D(WriteData), .en(AND_gate_4_out), .Q(reg3_q), .clk(clock));  // open: clr
  Register #(.width(32)) reg4 (.D(WriteData), .en(AND_gate_5_out), .Q(reg4_q), .clk(clock));  // open: clr
  Register #(.width(32)) reg5 (.D(WriteData), .en(AND_gate_6_out), .Q(reg5_q), .clk(clock));  // open: clr
  Register #(.width(32)) reg6 (.D(WriteData), .en(AND_gate_7_out), .Q(reg6_q), .clk(clock));  // open: clr
  Register #(.width(32)) reg7 (.D(WriteData), .en(AND_gate_8_out), .Q(reg7_q), .clk(clock));  // open: clr
  Register #(.width(32)) reg8 (.D(WriteData), .en(AND_gate_9_out), .Q(reg8_q), .clk(clock));  // open: clr
  Register #(.width(32)) reg9 (.D(WriteData), .en(AND_gate_10_out), .Q(reg9_q), .clk(clock));  // open: clr
  Register #(.width(32)) reg10 (.D(WriteData), .en(AND_gate_11_out), .Q(reg10_q), .clk(clock));  // open: clr
  Register #(.width(32)) reg11 (.D(WriteData), .en(AND_gate_12_out), .Q(reg11_q), .clk(clock));  // open: clr
  Register #(.width(32)) reg12 (.D(WriteData), .en(AND_gate_13_out), .Q(reg12_q), .clk(clock));  // open: clr
  Register #(.width(32)) reg13 (.D(WriteData), .en(AND_gate_14_out), .Q(reg13_q), .clk(clock));  // open: clr
  Register #(.width(32)) reg14 (.D(WriteData), .en(AND_gate_15_out), .Q(reg14_q), .clk(clock));  // open: clr
  Register #(.width(32)) reg15 (.D(WriteData), .en(AND_gate_16_out), .Q(reg15_q), .clk(clock));  // open: clr
  Register #(.width(32)) reg16 (.D(WriteData), .en(AND_gate_17_out), .Q(reg16_q), .clk(clock));  // open: clr
  Register #(.width(32)) reg17 (.D(WriteData), .en(AND_gate_18_out), .Q(reg17_q), .clk(clock));  // open: clr
  Register #(.width(32)) reg18 (.D(WriteData), .en(AND_gate_19_out), .Q(reg18_q), .clk(clock));  // open: clr
  Register #(.width(32)) reg19 (.D(WriteData), .en(AND_gate_20_out), .Q(reg19_q), .clk(clock));  // open: clr
  Register #(.width(32)) reg20 (.D(WriteData), .en(AND_gate_21_out), .Q(reg20_q), .clk(clock));  // open: clr
  Register #(.width(32)) reg21 (.D(WriteData), .en(AND_gate_22_out), .Q(reg21_q), .clk(clock));  // open: clr
  Register #(.width(32)) reg22 (.D(WriteData), .en(AND_gate_23_out), .Q(reg22_q), .clk(clock));  // open: clr
  Register #(.width(32)) reg23 (.D(WriteData), .en(AND_gate_24_out), .Q(reg23_q), .clk(clock));  // open: clr
  Register #(.width(32)) reg24 (.D(WriteData), .en(AND_gate_25_out), .Q(reg24_q), .clk(clock));  // open: clr
  Register #(.width(32)) reg25 (.D(WriteData), .en(AND_gate_26_out), .Q(reg25_q), .clk(clock));  // open: clr
  Register #(.width(32)) reg26 (.D(WriteData), .en(AND_gate_27_out), .Q(reg26_q), .clk(clock));  // open: clr
  Register #(.width(32)) reg27 (.D(WriteData), .en(AND_gate_28_out), .Q(reg27_q), .clk(clock));  // open: clr
  Register #(.width(32)) reg28 (.D(WriteData), .en(AND_gate_29_out), .Q(reg28_q), .clk(clock));  // open: clr
  Register #(.width(32)) reg29 (.D(WriteData), .en(AND_gate_30_out), .Q(reg29_q), .clk(clock));  // open: clr
  Register #(.width(32)) reg30 (.D(WriteData), .en(AND_gate_31_out), .Q(reg30_q), .clk(clock));  // open: clr
  Register #(.width(32)) reg31 (.D(WriteData), .en(AND_gate_32_out), .Q(reg31_q), .clk(clock));  // open: clr
  Multiplexer #(.select(5), .width(32), .enable("false")) multiplexer_1 (
    .in0(reg0_q), .in1(reg1_q), .in2(reg2_q), .in3(reg3_q), .in4(reg4_q), .in5(reg5_q), .in6(reg6_q),
    .in7(reg7_q), .in8(reg8_q), .in9(reg9_q), .in10(reg10_q), .in11(reg11_q), .in12(reg12_q), .in13(reg13_q),
    .in14(reg14_q), .in15(reg15_q), .in16(reg16_q), .in17(reg17_q), .in18(reg18_q), .in19(reg19_q),
    .in20(reg20_q), .in21(reg21_q), .in22(reg22_q), .in23(reg23_q), .in24(reg24_q), .in25(reg25_q),
    .in26(reg26_q), .in27(reg27_q), .in28(reg28_q), .in29(reg29_q), .in30(reg30_q), .in31(reg31_q),
    .out(ReadData1), .sel(ReadReg1));
  Multiplexer #(.select(5), .width(32), .enable("false")) multiplexer_2 (
    .in0(reg0_q), .in1(reg1_q), .in2(reg2_q), .in3(reg3_q), .in4(reg4_q), .in5(reg5_q), .in6(reg6_q),
    .in7(reg7_q), .in8(reg8_q), .in9(reg9_q), .in10(reg10_q), .in11(reg11_q), .in12(reg12_q), .in13(reg13_q),
    .in14(reg14_q), .in15(reg15_q), .in16(reg16_q), .in17(reg17_q), .in18(reg18_q), .in19(reg19_q),
    .in20(reg20_q), .in21(reg21_q), .in22(reg22_q), .in23(reg23_q), .in24(reg24_q), .in25(reg25_q),
    .in26(reg26_q), .in27(reg27_q), .in28(reg28_q), .in29(reg29_q), .in30(reg30_q), .in31(reg31_q),
    .out(ReadData2), .sel(ReadReg2));
endmodule
