// Logisim project SCDP.circ as structural Verilog: 9 circuits, main circuit main
module main (
  output zero,
  output zero_2
);

  wire ALUop0, ALUop1, ALUsrc, Branch, Clock_2_out, Clock_3_out, Clock_4_out, Clock_out, Jump, MemRead,
       MemToReg, MemWrite, RegDst, RegWrite;
  wire [2:0] ALUoperation;
  wire [4:0] multiplexer_1_out, multiplexer_2_out;
  wire [5:0] IF_2_ir;
  wire [15:0] IF_2_ir_3;
  wire [15:6] IF_2_ir_2;
  wire [23:0] bit_extender_3_out, bit_extender_4_out;
  wire [31:0] alu_1_aluresult, alu_2_aluresult, bit_extender_1_out, bit_extender_2_out,
       DataMemory_2_read_data, DataMemory_read_data, IF_ir, multiplexer_3_out, multiplexer_4_out,
       multiplexer_5_out, multiplexer_6_out, Register_File_2_readdata1, Register_File_2_readdata2,
       Register_File_readdata1, Register_File_readdata2;

  Clock Clock (.out(Clock_out));
  // Probe on IF_ir
  IFU IF (.CLOCK(Clock_out), .ENABLE(1'b1), .IR(IF_ir));
  // Probe on IF_ir
  // Probe on {IF_2_ir_3, IF_2_ir_2, IF_2_ir}
  Clock Clock_2 (.out(Clock_2_out));
  // Probe on {IF_2_ir_3, IF_2_ir_2, IF_2_ir}
  // Probe on IF_ir[20:16]
  // Probe on {IF_2_ir_3, IF_2_ir_2, IF_2_ir}
  IFU IF_2 (.CLOCK(Clock_2_out), .ENABLE(1'b1), .IR({IF_2_ir_3, IF_2_ir_2, IF_2_ir}));
  // Probe on {IF_2_ir_3, IF_2_ir_2, IF_2_ir}
  // Probe on IF_ir[20:16]
  Multiplexer #(.width(5), .enable("false")) multiplexer_1 (
    .in0(IF_ir[20:16]), .in1(IF_ir[15:11]), .out(multiplexer_1_out), .sel(1'b0));
  assign bit_extender_1_out = {{16{1'b0}}, IF_ir[15:0]};  // Bit_Extender bit_extender_1
  // Probe on {ALUop1, ALUop0}
  // Probe on IF_ir[25:21]
  // Probe on multiplexer_1_out
  MainCU MainCU (
    .OperationCode(IF_2_ir_3[15:10]), .RegWrite(RegWrite), .RegDst(RegDst), .ALUsrc(ALUsrc),
    .MemToReg(MemToReg), .MemRead(MemRead), .MemWrite(MemWrite), .Branch(Branch), .Jump(Jump),
    .ALUop1(ALUop1), .ALUop0(ALUop0));
  // Probe on IF_2_ir_3[9:5]
  // Probe on IF_2_ir_3[4:0]
  Multiplexer #(.width(5), .enable("false")) multiplexer_2 (
    .in0(IF_2_ir_3[4:0]), .in1(IF_2_ir_2[15:11]), .out(multiplexer_2_out), .sel(RegDst));
  // Probe on RegDst
  // Probe on RegWrite
  assign bit_extender_2_out = {{16{1'b0}}, {IF_2_ir_2, IF_2_ir}};  // Bit_Extender bit_extender_2
  ALU_CU ALU_CU (.ALU_op({ALUop1, ALUop0}), .FunctionCode(IF_2_ir), .ALUOperation(ALUoperation));
  // Probe on ALUoperation
  Read_Write_Ports Register_File (
    .ReadReg1(IF_ir[25:21]), .ReadReg2(IF_ir[20:16]), .WRITE(1'b1), .clock(Clock_out),
    .WriteRegister(multiplexer_1_out), .WriteData(multiplexer_5_out), .ReadData1(Register_File_readdata1),
    .ReadData2(Register_File_readdata2));
  // Probe on bit_extender_1_out
  // Probe on multiplexer_2_out
  // Probe on Register_File_readdata1
  // Probe on Register_File_readdata2
  Multiplexer #(.width(32), .enable("false")) multiplexer_3 (
    .in0(Register_File_readdata2), .in1(bit_extender_1_out), .out(multiplexer_3_out), .sel(1'b1));
  // Probe on Register_File_2_readdata1
  Read_Write_Ports Register_File_2 (
    .ReadReg1(IF_2_ir_3[9:5]), .ReadReg2(IF_2_ir_3[4:0]), .WRITE(RegWrite), .clock(Clock_2_out),
    .WriteRegister(multiplexer_2_out), .WriteData(multiplexer_6_out), .ReadData1(Register_File_2_readdata1),
    .ReadData2(Register_File_2_readdata2));
  // Probe on bit_extender_2_out
  ALU alu_1 (
    .ALUOperation(3'b010), .SRC1(Register_File_readdata1), .SRC2(multiplexer_3_out), .Zero(zero_2),
    .ALUResult(alu_1_aluresult));
  // Probe on multiplexer_3_out
  // Probe on Register_File_2_readdata2
  Multiplexer #(.width(32), .enable("false")) multiplexer_4 (
    .in0(Register_File_2_readdata2), .in1(bit_extender_2_out), .out(multiplexer_4_out), .sel(ALUsrc));
  // Probe on ALUsrc
  // Probe on multiplexer_6_out
  // Probe on alu_1_aluresult
  // Probe on ALUoperation
  ALU alu_2 (
    .ALUOperation(ALUoperation), .SRC1(Register_File_2_readdata1), .SRC2(multiplexer_4_out), .Zero(zero),
    .ALUResult(alu_2_aluresult));
  // Probe on multiplexer_4_out
  Bit_Extender #(.in_width(32), .out_width(24)) bit_extender_3 (.in(alu_1_aluresult), .out(bit_extender_3_out));
  Clock Clock_3 (.out(Clock_3_out));
  Bit_Extender #(.in_width(32), .out_width(24)) bit_extender_4 (.in(alu_2_aluresult), .out(bit_extender_4_out));
  // Probe on alu_2_aluresult
  // Probe on MemRead
  // Probe on MemWrite
  Clock Clock_4 (.out(Clock_4_out));
  // Probe on multiplexer_5_out
  Multiplexer #(.width(32), .enable("false")) multiplexer_5 (
    .in0(alu_1_aluresult), .in1(DataMemory_read_data), .out(multiplexer_5_out), .sel(1'b1));
  DATA_MEMORY DataMemory (
    .Address(bit_extender_3_out), .Write_Data(Register_File_readdata2), .MemRead(1'b0), .MemWrite(1'b1),
    .Clock(Clock_3_out), .Read_Data(DataMemory_read_data));
  // Probe on DataMemory_2_read_data
  // Probe on multiplexer_6_out
  Multiplexer #(.width(32), .enable("false")) multiplexer_6 (
    .in0(alu_2_aluresult), .in1(DataMemory_2_read_data), .out(multiplexer_6_out), .sel(MemToReg));
  DATA_MEMORY DataMemory_2 (
    .Address(bit_extender_4_out), .Write_Data(Register_File_2_readdata2), .MemRead(MemRead),
    .MemWrite(MemWrite), .Clock(Clock_4_out), .Read_Data(DataMemory_2_read_data));
  // Probe on MemToReg

  // Notes on the sheet:
  //   enable
  //   enable
  //   Func code
  //   RegDst
  //   operation code
  //   write
  //   Combined Datapath for R-type and Data Transfer Instructions
  //   ALUSrc
  //   ALUOperation
  //   Single Cycle Data Path
  //   MemRead
  //   MemWrite
  //   MemToReg
endmodule

module WritePort (
  input  WRITE,
  input  clock,
  input  [4:0] WriteRegister,
  input  [31:0] WriteData
);

  wire AND_gate_2_out, AND_gate_3_out, AND_gate_4_out, AND_gate_5_out, AND_gate_6_out, AND_gate_7_out,
       AND_gate_8_out, AND_gate_9_out, AND_gate_10_out, AND_gate_11_out, AND_gate_12_out, AND_gate_13_out,
       AND_gate_14_out, AND_gate_15_out, AND_gate_16_out, AND_gate_17_out, AND_gate_18_out, AND_gate_19_out,
       AND_gate_20_out, AND_gate_21_out, AND_gate_22_out, AND_gate_23_out, AND_gate_24_out, AND_gate_25_out,
       AND_gate_26_out, AND_gate_27_out, AND_gate_28_out, AND_gate_29_out, AND_gate_30_out, AND_gate_31_out,
       AND_gate_32_out, AND_gate_out, decoder_1_out0, decoder_1_out1, decoder_1_out2, decoder_1_out3,
       decoder_1_out4, decoder_1_out5, decoder_1_out6, decoder_1_out7, decoder_1_out8, decoder_1_out9,
       decoder_1_out10, decoder_1_out11, decoder_1_out12, decoder_1_out13, decoder_1_out14, decoder_1_out15,
       decoder_1_out16, decoder_1_out17, decoder_1_out18, decoder_1_out19, decoder_1_out20, decoder_1_out21,
       decoder_1_out22, decoder_1_out23, decoder_1_out24, decoder_1_out25, decoder_1_out26, decoder_1_out27,
       decoder_1_out28, decoder_1_out29, decoder_1_out30, decoder_1_out31;

  Decoder #(.select(5), .enable("false")) decoder_1 (
    .out0(decoder_1_out0), .out1(decoder_1_out1), .out2(decoder_1_out2), .out3(decoder_1_out3),
    .out4(decoder_1_out4), .out5(decoder_1_out5), .out6(decoder_1_out6), .out7(decoder_1_out7),
    .out8(decoder_1_out8), .out9(decoder_1_out9), .out10(decoder_1_out10), .out11(decoder_1_out11),
    .out12(decoder_1_out12), .out13(decoder_1_out13), .out14(decoder_1_out14), .out15(decoder_1_out15),
    .out16(decoder_1_out16), .out17(decoder_1_out17), .out18(decoder_1_out18), .out19(decoder_1_out19),
    .out20(decoder_1_out20), .out21(decoder_1_out21), .out22(decoder_1_out22), .out23(decoder_1_out23),
    .out24(decoder_1_out24), .out25(decoder_1_out25), .out26(decoder_1_out26), .out27(decoder_1_out27),
    .out28(decoder_1_out28), .out29(decoder_1_out29), .out30(decoder_1_out30), .out31(decoder_1_out31),
    .sel(WriteRegister));
  and AND_gate (AND_gate_out, WRITE, decoder_1_out0);
  and AND_gate_2 (AND_gate_2_out, WRITE, decoder_1_out1);
  and AND_gate_3 (AND_gate_3_out, WRITE, decoder_1_out2);
  and AND_gate_4 (AND_gate_4_out, WRITE, decoder_1_out3);
  and AND_gate_5 (AND_gate_5_out, WRITE, decoder_1_out4);
  and AND_gate_6 (AND_gate_6_out, WRITE, decoder_1_out5);
  and AND_gate_7 (AND_gate_7_out, WRITE, decoder_1_out6);
  and AND_gate_8 (AND_gate_8_out, WRITE, decoder_1_out7);
  and AND_gate_9 (AND_gate_9_out, WRITE, decoder_1_out8);
  and AND_gate_10 (AND_gate_10_out, WRITE, decoder_1_out9);
  and AND_gate_11 (AND_gate_11_out, WRITE, decoder_1_out10);
  and AND_gate_12 (AND_gate_12_out, WRITE, decoder_1_out11);
  and AND_gate_13 (AND_gate_13_out, WRITE, decoder_1_out12);
  and AND_gate_14 (AND_gate_14_out, WRITE, decoder_1_out13);
  and AND_gate_15 (AND_gate_15_out, WRITE, decoder_1_out14);
  and AND_gate_16 (AND_gate_16_out, WRITE, decoder_1_out15);
  and AND_gate_17 (AND_gate_17_out, WRITE, decoder_1_out16);
  and AND_gate_18 (AND_gate_18_out, WRITE, decoder_1_out17);
  and AND_gate_19 (AND_gate_19_out, WRITE, decoder_1_out18);
  and AND_gate_20 (AND_gate_20_out, WRITE, decoder_1_out19);
  and AND_gate_21 (AND_gate_21_out, WRITE, decoder_1_out20);
  and AND_gate_22 (AND_gate_22_out, WRITE, decoder_1_out21);
  and AND_gate_23 (AND_gate_23_out, WRITE, decoder_1_out22);
  and AND_gate_24 (AND_gate_24_out, WRITE, decoder_1_out23);
  and AND_gate_25 (AND_gate_25_out, WRITE, decoder_1_out24);
  and AND_gate_26 (AND_gate_26_out, WRITE, decoder_1_out25);
  and AND_gate_27 (AND_gate_27_out, WRITE, decoder_1_out26);
  and AND_gate_28 (AND_gate_28_out, WRITE, decoder_1_out27);
  and AND_gate_29 (AND_gate_29_out, WRITE, decoder_1_out28);
  and AND_gate_30 (AND_gate_30_out, WRITE, decoder_1_out29);
  and AND_gate_31 (AND_gate_31_out, WRITE, decoder_1_out30);
  and AND_gate_32 (AND_gate_32_out, WRITE, decoder_1_out31);
  Register #(.width(32)) reg0 (.D(WriteData), .en(AND_gate_out), .clk(clock));  // open: Q, clr
  Register #(.width(32)) reg1 (.D(WriteData), .en(AND_gate_2_out), .clk(clock));  // open: Q, clr
  Register #(.width(32)) reg2 (.D(WriteData), .en(AND_gate_3_out), .clk(clock));  // open: Q, clr
  Register #(.width(32)) reg3 (.D(WriteData), .en(AND_gate_4_out), .clk(clock));  // open: Q, clr
  Register #(.width(32)) reg4 (.D(WriteData), .en(AND_gate_5_out), .clk(clock));  // open: Q, clr
  Register #(.width(32)) reg5 (.D(WriteData), .en(AND_gate_6_out), .clk(clock));  // open: Q, clr
  Register #(.width(32)) reg6 (.D(WriteData), .en(AND_gate_7_out), .clk(clock));  // open: Q, clr
  Register #(.width(32)) reg7 (.D(WriteData), .en(AND_gate_8_out), .clk(clock));  // open: Q, clr
  Register #(.width(32)) reg8 (.D(WriteData), .en(AND_gate_9_out), .clk(clock));  // open: Q, clr
  Register #(.width(32)) reg9 (.D(WriteData), .en(AND_gate_10_out), .clk(clock));  // open: Q, clr
  Register #(.width(32)) reg10 (.D(WriteData), .en(AND_gate_11_out), .clk(clock));  // open: Q, clr
  Register #(.width(32)) reg11 (.D(WriteData), .en(AND_gate_12_out), .clk(clock));  // open: Q, clr
  Register #(.width(32)) reg12 (.D(WriteData), .en(AND_gate_13_out), .clk(clock));  // open: Q, clr
  Register #(.width(32)) reg13 (.D(WriteData), .en(AND_gate_14_out), .clk(clock));  // open: Q, clr
  Register #(.width(32)) reg14 (.D(WriteData), .en(AND_gate_15_out), .clk(clock));  // open: Q, clr
  Register #(.width(32)) reg15 (.D(WriteData), .en(AND_gate_16_out), .clk(clock));  // open: Q, clr
  Register #(.width(32)) reg16 (.D(WriteData), .en(AND_gate_17_out), .clk(clock));  // open: Q, clr
  Register #(.width(32)) reg17 (.D(WriteData), .en(AND_gate_18_out), .clk(clock));  // open: Q, clr
  Register #(.width(32)) reg18 (.D(WriteData), .en(AND_gate_19_out), .clk(clock));  // open: Q, clr
  Register #(.width(32)) reg19 (.D(WriteData), .en(AND_gate_20_out), .clk(clock));  // open: Q, clr
  Register #(.width(32)) reg20 (.D(WriteData), .en(AND_gate_21_out), .clk(clock));  // open: Q, clr
  Register #(.width(32)) reg21 (.D(WriteData), .en(AND_gate_22_out), .clk(clock));  // open: Q, clr
  Register #(.width(32)) reg22 (.D(WriteData), .en(AND_gate_23_out), .clk(clock));  // open: Q, clr
  Register #(.width(32)) reg23 (.D(WriteData), .en(AND_gate_24_out), .clk(clock));  // open: Q, clr
  Register #(.width(32)) reg24 (.D(WriteData), .en(AND_gate_25_out), .clk(clock));  // open: Q, clr
  Register #(.width(32)) reg25 (.D(WriteData), .en(AND_gate_26_out), .clk(clock));  // open: Q, clr
  Register #(.width(32)) reg26 (.D(WriteData), .en(AND_gate_27_out), .clk(clock));  // open: Q, clr
  Register #(.width(32)) reg27 (.D(WriteData), .en(AND_gate_28_out), .clk(clock));  // open: Q, clr
  Register #(.width(32)) reg28 (.D(WriteData), .en(AND_gate_29_out), .clk(clock));  // open: Q, clr
  Register #(.width(32)) reg29 (.D(WriteData), .en(AND_gate_30_out), .clk(clock));  // open: Q, clr
  Register #(.width(32)) reg30 (.D(WriteData), .en(AND_gate_31_out), .clk(clock));  // open: Q, clr
  Register #(.width(32)) reg31 (.D(WriteData), .en(AND_gate_32_out), .clk(clock));  // open: Q, clr
endmodule

module Read_Write_Ports (
  input  [4:0] ReadReg1,
  input  [4:0] ReadReg2,
  input  WRITE,
  input  clock,
  input  [4:0] WriteRegister,
  input  [31:0] WriteData,
  output [31:0] ReadData1,
  output [31:0] ReadData2
);

  wire AND_gate_2_out, AND_gate_3_out, AND_gate_4_out, AND_gate_5_out, AND_gate_6_out, AND_gate_7_out,
       AND_gate_8_out, AND_gate_9_out, AND_gate_10_out, AND_gate_11_out, AND_gate_12_out, AND_gate_13_out,
       AND_gate_14_out, AND_gate_15_out, AND_gate_16_out, AND_gate_17_out, AND_gate_18_out, AND_gate_19_out,
       AND_gate_20_out, AND_gate_21_out, AND_gate_22_out, AND_gate_23_out, AND_gate_24_out, AND_gate_25_out,
       AND_gate_26_out, AND_gate_27_out, AND_gate_28_out, AND_gate_29_out, AND_gate_30_out, AND_gate_31_out,
       AND_gate_32_out, AND_gate_out, decoder_1_out0, decoder_1_out1, decoder_1_out2, decoder_1_out3,
       decoder_1_out4, decoder_1_out5, decoder_1_out6, decoder_1_out7, decoder_1_out8, decoder_1_out9,
       decoder_1_out10, decoder_1_out11, decoder_1_out12, decoder_1_out13, decoder_1_out14, decoder_1_out15,
       decoder_1_out16, decoder_1_out17, decoder_1_out18, decoder_1_out19, decoder_1_out20, decoder_1_out21,
       decoder_1_out22, decoder_1_out23, decoder_1_out24, decoder_1_out25, decoder_1_out26, decoder_1_out27,
       decoder_1_out28, decoder_1_out29, decoder_1_out30, decoder_1_out31;
  wire [31:0] reg0_q, reg1_q, reg2_q, reg3_q, reg4_q, reg5_q, reg6_q, reg7_q, reg8_q, reg9_q, reg10_q,
       reg11_q, reg12_q, reg13_q, reg14_q, reg15_q, reg16_q, reg17_q, reg18_q, reg19_q, reg20_q, reg21_q,
       reg22_q, reg23_q, reg24_q, reg25_q, reg26_q, reg27_q, reg28_q, reg29_q, reg30_q, reg31_q;

  Decoder #(.select(5), .enable("false")) decoder_1 (
    .out0(decoder_1_out0), .out1(decoder_1_out1), .out2(decoder_1_out2), .out3(decoder_1_out3),
    .out4(decoder_1_out4), .out5(decoder_1_out5), .out6(decoder_1_out6), .out7(decoder_1_out7),
    .out8(decoder_1_out8), .out9(decoder_1_out9), .out10(decoder_1_out10), .out11(decoder_1_out11),
    .out12(decoder_1_out12), .out13(decoder_1_out13), .out14(decoder_1_out14), .out15(decoder_1_out15),
    .out16(decoder_1_out16), .out17(decoder_1_out17), .out18(decoder_1_out18), .out19(decoder_1_out19),
    .out20(decoder_1_out20), .out21(decoder_1_out21), .out22(decoder_1_out22), .out23(decoder_1_out23),
    .out24(decoder_1_out24), .out25(decoder_1_out25), .out26(decoder_1_out26), .out27(decoder_1_out27),
    .out28(decoder_1_out28), .out29(decoder_1_out29), .out30(decoder_1_out30), .out31(decoder_1_out31),
    .sel(WriteRegister));
  and AND_gate (AND_gate_out, WRITE, decoder_1_out0);
  and AND_gate_2 (AND_gate_2_out, WRITE, decoder_1_out1);
  and AND_gate_3 (AND_gate_3_out, WRITE, decoder_1_out2);
  and AND_gate_4 (AND_gate_4_out, WRITE, decoder_1_out3);
  and AND_gate_5 (AND_gate_5_out, WRITE, decoder_1_out4);
  and AND_gate_6 (AND_gate_6_out, WRITE, decoder_1_out5);
  and AND_gate_7 (AND_gate_7_out, WRITE, decoder_1_out6);
  and AND_gate_8 (AND_gate_8_out, WRITE, decoder_1_out7);
  and AND_gate_9 (AND_gate_9_out, WRITE, decoder_1_out8);
  and AND_gate_10 (AND_gate_10_out, WRITE, decoder_1_out9);
  and AND_gate_11 (AND_gate_11_out, WRITE, decoder_1_out10);
  and AND_gate_12 (AND_gate_12_out, WRITE, decoder_1_out11);
  and AND_gate_13 (AND_gate_13_out, WRITE, decoder_1_out12);
  and AND_gate_14 (AND_gate_14_out, WRITE, decoder_1_out13);
  and AND_gate_15 (AND_gate_15_out, WRITE, decoder_1_out14);
  and AND_gate_16 (AND_gate_16_out, WRITE, decoder_1_out15);
  and AND_gate_17 (AND_gate_17_out, WRITE, decoder_1_out16);
  and AND_gate_18 (AND_gate_18_out, WRITE, decoder_1_out17);
  and AND_gate_19 (AND_gate_19_out, WRITE, decoder_1_out18);
  and AND_gate_20 (AND_gate_20_out, WRITE, decoder_1_out19);
  and AND_gate_21 (AND_gate_21_out, WRITE, decoder_1_out20);
  and AND_gate_22 (AND_gate_22_out, WRITE, decoder_1_out21);
  and AND_gate_23 (AND_gate_23_out, WRITE, decoder_1_out22);
  and AND_gate_24 (AND_gate_24_out, WRITE, decoder_1_out23);
  and AND_gate_25 (AND_gate_25_out, WRITE, decoder_1_out24);
  and AND_gate_26 (AND_gate_26_out, WRITE, decoder_1_out25);
  and AND_gate_27 (AND_gate_27_out, WRITE, decoder_1_out26);
  and AND_gate_28 (AND_gate_28_out, WRITE, decoder_1_out27);
  and AND_gate_29 (AND_gate_29_out, WRITE, decoder_1_out28);
  and AND_gate_30 (AND_gate_30_out, WRITE, decoder_1_out29);
  and AND_gate_31 (AND_gate_31_out, WRITE, decoder_1_out30);
  and AND_gate_32 (AND_gate_32_out, WRITE, decoder_1_out31);
  Register #(.width(32)) reg0 (.D(WriteData), .en(AND_gate_out), .Q(reg0_q), .clk(clock));  // open: clr
  Register #(.width(32)) reg1 (.D(WriteData), .en(AND_gate_2_out), .Q(reg1_q), .clk(clock));  // open: clr
  Register #(.width(32)) reg2 (.D(WriteData), .en(AND_gate_3_out), .Q(reg2_q), .clk(clock));  // open: clr
  Register #(.width(32)) reg3 (.D(WriteData), .en(AND_gate_4_out), .Q(reg3_q), .clk(clock));  // open: clr
  Register #(.width(32)) reg4 (.D(WriteData), .en(AND_gate_5_out), .Q(reg4_q), .clk(clock));  // open: clr
  Register #(.width(32)) reg5 (.D(WriteData), .en(AND_gate_6_out), .Q(reg5_q), .clk(clock));  // open: clr
  Register #(.width(32)) reg6 (.D(WriteData), .en(AND_gate_7_out), .Q(reg6_q), .clk(clock));  // open: clr
  Register #(.width(32)) reg7 (.D(WriteData), .en(AND_gate_8_out), .Q(reg7_q), .clk(clock));  // open: clr
  Register #(.width(32)) reg8 (.D(WriteData), .en(AND_gate_9_out), .Q(reg8_q), .clk(clock));  // open: clr
  Register #(.width(32)) reg9 (.D(WriteData), .en(AND_gate_10_out), .Q(reg9_q), .clk(clock));  // open: clr
  Register #(.width(32)) reg10 (.D(WriteData), .en(AND_gate_11_out), .Q(reg10_q), .clk(clock));  // open: clr
  Register #(.width(32)) reg11 (.D(WriteData), .en(AND_gate_12_out), .Q(reg11_q), .clk(clock));  // open: clr
  Register #(.width(32)) reg12 (.D(WriteData), .en(AND_gate_13_out), .Q(reg12_q), .clk(clock));  // open: clr
  Register #(.width(32)) reg13 (.D(WriteData), .en(AND_gate_14_out), .Q(reg13_q), .clk(clock));  // open: clr
  Register #(.width(32)) reg14 (.D(WriteData), .en(AND_gate_15_out), .Q(reg14_q), .clk(clock));  // open: clr
  Register #(.width(32)) reg15 (.D(WriteData), .en(AND_gate_16_out), .Q(reg15_q), .clk(clock));  // open: clr
  Register #(.width(32)) reg16 (.D(WriteData), .en(AND_gate_17_out), .Q(reg16_q), .clk(clock));  // open: clr
  Register #(.width(32)) reg17 (.D(WriteData), .en(AND_gate_18_out), .Q(reg17_q), .clk(clock));  // open: clr
  Register #(.width(32)) reg18 (.D(WriteData), .en(AND_gate_19_out), .Q(reg18_q), .clk(clock));  // open: clr
  Register #(.width(32)) reg19 (.D(WriteData), .en(AND_gate_20_out), .Q(reg19_q), .clk(clock));  // open: clr
  Register #(.width(32)) reg20 (.D(WriteData), .en(AND_gate_21_out), .Q(reg20_q), .clk(clock));  // open: clr
  Register #(.width(32)) reg21 (.D(WriteData), .en(AND_gate_22_out), .Q(reg21_q), .clk(clock));  // open: clr
  Register #(.width(32)) reg22 (.D(WriteData), .en(AND_gate_23_out), .Q(reg22_q), .clk(clock));  // open: clr
  Register #(.width(32)) reg23 (.D(WriteData), .en(AND_gate_24_out), .Q(reg23_q), .clk(clock));  // open: clr
  Register #(.width(32)) reg24 (.D(WriteData), .en(AND_gate_25_out), .Q(reg24_q), .clk(clock));  // open: clr
  Register #(.width(32)) reg25 (.D(WriteData), .en(AND_gate_26_out), .Q(reg25_q), .clk(clock));  // open: clr
  Register #(.width(32)) reg26 (.D(WriteData), .en(AND_gate_27_out), .Q(reg26_q), .clk(clock));  // open: clr
  Register #(.width(32)) reg27 (.D(WriteData), .en(AND_gate_28_out), .Q(reg27_q), .clk(clock));  // open: clr
  Register #(.width(32)) reg28 (.D(WriteData), .en(AND_gate_29_out), .Q(reg28_q), .clk(clock));  // open: clr
  Register #(.width(32)) reg29 (.D(WriteData), .en(AND_gate_30_out), .Q(reg29_q), .clk(clock));  // open: clr
  Register #(.width(32)) reg30 (.D(WriteData), .en(AND_gate_31_out), .Q(reg30_q), .clk(clock));  // open: clr
  Register #(.width(32)) reg31 (.D(WriteData), .en(AND_gate_32_out), .Q(reg31_q), .clk(clock));  // open: clr
  Multiplexer #(.select(5), .width(32), .enable("false")) multiplexer_1 (
    .in0(reg0_q), .in1(reg1_q), .in2(reg2_q), .in3(reg3_q), .in4(reg4_q), .in5(reg5_q), .in6(reg6_q),
    .in7(reg7_q), .in8(reg8_q), .in9(reg9_q), .in10(reg10_q), .in11(reg11_q), .in12(reg12_q), .in13(reg13_q),
    .in14(reg14_q), .in15(reg15_q), .in16(reg16_q), .in17(reg17_q), .in18(reg18_q), .in19(reg19_q),
    .in20(reg20_q), .in21(reg21_q), .in22(reg22_q), .in23(reg23_q), .in24(reg24_q), .in25(reg25_q),
    .in26(reg26_q), .in27(reg27_q), .in28(reg28_q), .in29(reg29_q), .in30(reg30_q), .in31(reg31_q),
    .out(ReadData1), .sel(ReadReg1));
  Multiplexer #(.select(5), .width(32), .enable("false")) multiplexer_2 (
    .in0(reg0_q), .in1(reg1_q), .in2(reg2_q), .in3(reg3_q), .in4(reg4_q), .in5(reg5_q), .in6(reg6_q),
    .in7(reg7_q), .in8(reg8_q), .in9(reg9_q), .in10(reg10_q), .in11(reg11_q), .in12(reg12_q), .in13(reg13_q),
    .in14(reg14_q), .in15(reg15_q), .in16(reg16_q), .in17(reg17_q), .in18(reg18_q), .in19(reg19_q),
    .in20(reg20_q), .in21(reg21_q), .in22(reg22_q), .in23(reg23_q), .in24(reg24_q), .in25(reg25_q),
    .in26(reg26_q), .in27(reg27_q), .in28(reg28_q), .in29(reg29_q), .in30(reg30_q), .in31(reg31_q),
    .out(ReadData2), .sel(ReadReg2));
endmodule

// IF
module IFU (
  input  CLOCK,
  input  ENABLE,
  output [31:0] IR
);

  wire [31:0] adder_1_out, PC_q;

  Register #(.width(32)) PC (.D(adder_1_out), .Q(PC_q), .clk(CLOCK));  // open: en, clr
  Adder #(.width(32)) adder_1 (.a(PC_q), .b(32'h1), .out(adder_1_out));  // open: cin, cout
  RAM #(.addrWidth(24), .dataWidth(32)) ram_1 (
    .addr(PC_q[23:0]), .data(IR), .clk(CLOCK), .ld(ENABLE));  // open: sel, clr

  // Notes on the sheet:
  //   Adder
  //   Instruction Memory
endmodule

module ALU (
  input  [2:0] ALUOperation,
  input  [31:0] SRC1,
  input  [31:0] SRC2,
  output Zero,
  output [31:0] ALUResult
);

  wire AND_2_out;
  wire [31:0] adder_1_out, adder_2_out, adder_3_out, AND_out, bit_extender_1_out, NOR_out, NOT_2_out,
       NOT_out, OR_out;

  assign NOT_out = ~SRC2;  // NOT_Gate NOT, 32 bits wide
  assign NOT_2_out = ~SRC2;  // NOT_Gate NOT_2, 32 bits wide
  assign AND_out = SRC1 & SRC2;  // AND_Gate AND, 32 bits wide
  assign OR_out = SRC1 | SRC2;  // OR_Gate OR, 32 bits wide
  Adder #(.width(32)) adder_1 (.a(SRC1), .b(SRC2), .out(adder_1_out));  // open: cin, cout
  Adder #(.width(32)) adder_2 (.a(SRC1), .b(NOT_out), .out(adder_2_out), .cin(1'b1));  // open: cout
  Adder #(.width(32)) adder_3 (.a(SRC1), .b(NOT_2_out), .out(adder_3_out), .cin(1'b1));  // open: cout
  and AND_2 (AND_2_out, adder_3_out[31], 1'b1);
  assign bit_extender_1_out = {{31{1'b0}}, AND_2_out};  // Bit_Extender bit_extender_1
  Multiplexer #(.select(3), .width(32), .enable("false")) multiplexer_1 (
    .in0(AND_out), .in1(OR_out), .in2(adder_1_out), .in6(adder_2_out), .in7(bit_extender_1_out),
    .out(ALUResult), .sel(ALUOperation));  // open: in3, in4, in5
  assign NOR_out = ~({32{1'b0}} | ALUResult);  // NOR_Gate NOR, 32 bits wide
  Bit_Extender #(.in_width(32), .out_width(1)) bit_extender_2 (.in(NOR_out), .out(Zero));

  // Notes on the sheet:
  //   Adder
  //   Subtractor
  //   slt
endmodule

module DATA_MEMORY (
  input  [23:0] Address,
  input  [31:0] Write_Data,
  input  MemRead,
  input  MemWrite,
  input  Clock,
  output [31:0] Read_Data
);

  RAM #(.addrWidth(24), .dataWidth(32), .bus("separate")) ram_1 (
    .addr(Address), .din(Write_Data), .data(Read_Data), .str(MemWrite), .clk(Clock), .ld(MemRead));  // open: sel, clr

  // Notes on the sheet:
  //   Data Memory
endmodule

module MainCU (
  input  [5:0] OperationCode,
  output RegWrite,
  output ALUsrc,
  output MemRead,
  output Branch,
  output ALUop1,
  output RegDst,
  output MemToReg,
  output MemWrite,
  output Jump,
  output ALUop0
);

  wire not_1_out, not_2_out, not_3_out, not_4_out, not_5_out, not_6_out;

  not not_1 (not_1_out, OperationCode[5]);
  not not_2 (not_2_out, OperationCode[4]);
  not not_3 (not_3_out, OperationCode[3]);
  not not_4 (not_4_out, OperationCode[2]);
  not not_5 (not_5_out, OperationCode[1]);
  not not_6 (not_6_out, OperationCode[0]);
  and R (ALUop1, not_6_out, not_5_out, not_4_out, not_3_out, not_2_out, not_1_out);
  and lw (MemRead, OperationCode[0], OperationCode[1], not_4_out, not_3_out, not_2_out, OperationCode[5]);
  and sw (MemWrite, OperationCode[0], OperationCode[1], not_4_out, OperationCode[3], not_2_out, OperationCode[5]);
  and beq (ALUop0, not_6_out, not_5_out, OperationCode[2], not_3_out, not_2_out, not_1_out);
  and j (Jump, not_6_out, OperationCode[1], not_4_out, not_3_out, not_2_out, not_1_out);
  or or_1 (RegWrite, ALUop1, MemRead);
  or or_2 (ALUsrc, MemRead, MemWrite);

  assign Branch = ALUop0;
  assign MemToReg = MemRead;
  assign RegDst = ALUop1;

  // Notes on the sheet:
  //   op5
  //   op4
  //   op3
  //   op1
  //   op2
  //   op0
endmodule

module ALU_CU (
  input  [1:0] ALU_op,
  input  [5:0] FunctionCode,
  output [2:0] ALUOperation
);

  wire and_1_out, not_1_out, not_2_out, or_1_out;

  or or_1 (or_1_out, FunctionCode[0], FunctionCode[3]);
  and and_1 (and_1_out, ALU_op[1], FunctionCode[1]);
  and and_2 (ALUOperation[0], ALU_op[1], or_1_out);
  or or_2 (ALUOperation[2], ALU_op[0], and_1_out);
  not not_1 (not_1_out, ALU_op[1]);
  or or_3 (ALUOperation[1], not_1_out, not_2_out);
  not not_2 (not_2_out, FunctionCode[2]);

  // Notes on the sheet:
  //   Operation0
  //   Operation2
  //   Operation1
endmodule

module sub_circuits (
  output [31:0] IR,
  output [31:0] ReadData1,
  output [31:0] ReadData2,
  output zero
);

  wire Clock_2_out, Clock_out;
  wire [31:0] alu_1_aluresult, IF_ir, Register_File_2_readdata1, Register_File_2_readdata2;

  Clock Clock (.out(Clock_out));
  Clock Clock_2 (.out(Clock_2_out));
  IFU IF (.CLOCK(Clock_out), .ENABLE(1'b1), .IR(IF_ir));
  IFU IF_2 (.CLOCK(Clock_2_out), .ENABLE(1'b1), .IR(IR));
  // Probe on IF_ir
  // Probe on IF_ir[25:21]
  // Probe on IF_ir[20:16]
  // Probe on IF_ir[15:11]
  Read_Write_Ports Register_File (
    .ReadReg1(IR[25:21]), .ReadReg2(IR[20:16]), .WRITE(1'b0), .clock(Clock_2_out), .WriteRegister(IR[15:11]),
    .WriteData(32'h55f9), .ReadData1(ReadData1), .ReadData2(ReadData2));
  Read_Write_Ports Register_File_2 (
    .ReadReg1(IF_ir[25:21]), .ReadReg2(IF_ir[20:16]), .WRITE(1'b1), .clock(Clock_out),
    .WriteRegister(IF_ir[15:11]), .WriteData(32'h9), .ReadData1(Register_File_2_readdata1),
    .ReadData2(Register_File_2_readdata2));
  // Probe on Register_File_2_readdata1
  // Probe on Register_File_2_readdata2
  ALU alu_1 (
    .ALUOperation(3'b010), .SRC1(Register_File_2_readdata1), .SRC2(Register_File_2_readdata2), .Zero(zero),
    .ALUResult(alu_1_aluresult));
  // Probe on alu_1_aluresult

  // Notes on the sheet:
  //   enable
  //   enable
  //   write
  //   WriteData
  //   WriteData
  //   Instruction Fetch Sub-circuit with Register File
  //   write
  //   Instruction Fetch , Register File and ALU sub-circuits
  //   ALUOperation
endmodule
