// Logisim project datamem.circ as structural Verilog: 2 circuits, main circuit main
module main (
);

  wire Clock_out;
  wire [31:0] Data_Memory_read_data;

  Clock Clock (.out(Clock_out));
  DATAMEM Data_Memory (
    .Address(24'h1), .Write_Data({32{1'b1}}), .MemRead(1'b1), .MemWrite(1'b1), .Clock(Clock_out),
    .Read_Data(Data_Memory_read_data));
  // Probe on Data_Memory_read_data

  // Notes on the sheet:
  //   Write Data
  //   Mem Read
  //   Mem Write
  //   Address
endmodule

module DATAMEM (
  input  [23:0] Address,
  input  [31:0] Write_Data,
  input  MemRead,
  input  MemWrite,
  input  Clock,
  output [31:0] Read_Data
);

  RAM #(.addrWidth(24), .dataWidth(32), .bus("separate")) ram_1 (
    .addr(Address), .din(Write_Data), .data(Read_Data), .str(MemWrite), .clk(Clock), .ld(MemRead));  // open: sel, clr

  // Notes on the sheet:
  //   Data Memory
endmodule
