// Logisim project mainCU.circ as structural Verilog: 2 circuits, main circuit main
module main (
  output RegWrite,
  output RegDst,
  output ALUsrc,
  output MemToReg,
  output MemRead,
  output MemWrite,
  output Branch,
  output Jump,
  output ALUop1,
  output ALUop0
);

  MainCU MainCU (
    .OperationCode(6'b000010), .RegWrite(RegWrite), .RegDst(RegDst), .ALUsrc(ALUsrc), .MemToReg(MemToReg),
    .MemRead(MemRead), .MemWrite(MemWrite), .Branch(Branch), .Jump(Jump), .ALUop1(ALUop1), .ALUop0(ALUop0));

  // Notes on the sheet:
  //   OperationCode
endmodule

module MainCU (
  input  [5:0] OperationCode,
  output RegWrite,
  output ALUsrc,
  output MemRead,
  output Branch,
  output ALUop1,
  output RegDst,
  output MemToReg,
  output MemWrite,
  output Jump,
  output ALUop0
);

  wire not_1_out, not_2_out, not_3_out, not_4_out, not_5_out, not_6_out;

  not not_1 (not_1_out, OperationCode[5]);
  not not_2 (not_2_out, OperationCode[4]);
  not not_3 (not_3_out, OperationCode[3]);
  not not_4 (not_4_out, OperationCode[2]);
  not not_5 (not_5_out, OperationCode[1]);
  not not_6 (not_6_out, OperationCode[0]);
  and R (ALUop1, not_6_out, not_5_out, not_4_out, not_3_out, not_2_out, not_1_out);
  and lw (MemRead, OperationCode[0], OperationCode[1], not_4_out, not_3_out, not_2_out, OperationCode[5]);
  and sw (MemWrite, OperationCode[0], OperationCode[1], not_4_out, OperationCode[3], not_2_out, OperationCode[5]);
  and beq (ALUop0, not_6_out, not_5_out, OperationCode[2], not_3_out, not_2_out, not_1_out);
  and j (Jump, not_6_out, OperationCode[1], not_4_out, not_3_out, not_2_out, not_1_out);
  or or_1 (RegWrite, ALUop1, MemRead);
  or or_2 (ALUsrc, MemRead, MemWrite);

  assign Branch = ALUop0;
  assign MemToReg = MemRead;
  assign RegDst = ALUop1;

  // Notes on the sheet:
  //   OperationCode: pull=down
  //   op5
  //   op4
  //   op3
  //   op1
  //   op2
  //   op0
endmodule
